// Logisim project cpu.circ as structural Verilog: 4 circuits, main circuit main
module main (
  input  [31:0] INSTRUCTION,
  input  CLOCK,
  output [31:0] FETCH_ADDRESS,
  output [31:0] ra,
  output [31:0] sp,
  output [31:0] t0,
  output [31:0] t1,
  output [31:0] t2,
  output [31:0] s0,
  output [31:0] s1,
  output [31:0] a0
);

  wire ASel, BrEq, BrLt, BrUn, BSel, MemRW, PCSel, RegWEn;
  wire [1:0] WBSel;
  wire [2:0] funct3, ImmSel;
  wire [3:0] ALUSel;
  wire [7:0] Byte;
  wire [15:0] Half;
  wire [31:0] A, ALUResult, B, ByteSX, ByteZX, HalfSX, HalfZX, imm, inst, MemRead, MemResult, MemWrite,
       multiplexer_1_out, multiplexer_2_out, PC, PC_4, PC_IF, PC_IF_4, R1, WB;

  Multiplexer #(.width(32), .enable("false")) multiplexer_1 (
    .in0(PC_IF_4), .in1(ALUResult), .out(multiplexer_1_out), .sel(PCSel));
  Register #(.width(32)) u_PC (.D(multiplexer_1_out), .en(1'b1), .clk(CLOCK), .Q(PC_IF));  // open: clr
  Register #(.width(32)) register_1 (
    .D(multiplexer_2_out), .en(1'b1), .clk(CLOCK), .Q({inst[31:15], funct3, inst[11:0]}));  // open: clr
  Multiplexer #(.width(32), .enable("false")) multiplexer_2 (
    .in0(INSTRUCTION), .in1(32'h13), .out(multiplexer_2_out), .sel(PCSel));
  Register #(.width(32)) register_2 (.D(PC_IF_4), .en(1'b1), .clk(CLOCK), .Q(PC_4));  // open: clr
  Register #(.width(32)) register_3 (.D(PC_IF), .en(1'b1), .clk(CLOCK), .Q(PC));  // open: clr
  assign FETCH_ADDRESS = {{2{1'b0}}, PC_IF[31:2]};  // Bit_Extender bit_extender_1
  Adder #(.width(32)) adder_1 (.a(PC_IF), .b(32'h4), .out(PC_IF_4));  // open: cin, cout
  brcomp brcomp_1 (.A(R1), .B(MemWrite), .BrUn(BrUn), .BrEQ(BrEq), .BrLt(BrLt));
  // Probe on imm
  immgen immgen_1 (.inst({inst[31:15], funct3, inst[11:0]}), .ImmSel(ImmSel), .imm(imm));
  control control_1 (
    .BrEq(BrEq), .BrLt(BrLt), .inst({inst[31:15], funct3, inst[11:0]}), .ImmSel(ImmSel), .BrUn(BrUn),
    .ASel(ASel), .BSel(BSel), .ALUSel(ALUSel), .MemRW(MemRW), .RegWEn(RegWEn), .WBSel(WBSel), .PCSel(PCSel));
  regfile_main RegFile (
    .rs2(inst[24:20]), .rd(inst[11:7]), .Read_Data_1(R1), .Read_Data_2(MemWrite), .ra(ra), .sp(sp), .t0(t0),
    .t1(t1), .t2(t2), .s0(s0), .s1(s1), .a0(a0), .rs1(inst[19:15]), .Write_Data(WB), .RegWEn(RegWEn),
    .clk(CLOCK));
  // Probe on MemWrite
  Multiplexer #(.width(32), .enable("false")) multiplexer_3 (.in0(R1), .in1(PC), .out(A), .sel(ASel));
  Multiplexer #(.width(32), .enable("false")) multiplexer_4 (.in0(MemWrite), .in1(imm), .out(B), .sel(BSel));
  alu Arithmetic_Logic_Unit (.A(A), .B(B), .ALUSel(ALUSel), .Result(ALUResult));
  // Probe on ALUResult
  Multiplexer #(.select(2), .width(32), .enable("false")) multiplexer_5 (
    .in0(MemResult), .in1(ALUResult), .in2(PC_4), .out(WB), .sel(WBSel));  // open: in3
  BitSelector #(.width(32), .group(8)) bitselector_1 (.in(MemRead), .out(Byte), .sel(ALUResult[1:0]));
  BitSelector #(.width(32), .group(16)) bitselector_2 (.in(MemRead), .out(Half), .sel(ALUResult[1]));
  assign ByteSX = {{24{Byte[7]}}, Byte};  // Bit_Extender bit_extender_2
  assign ByteZX = {{24{1'b0}}, Byte};  // Bit_Extender bit_extender_3
  assign HalfSX = {{16{Half[15]}}, Half};  // Bit_Extender bit_extender_4
  assign HalfZX = {{16{1'b0}}, Half};  // Bit_Extender bit_extender_5
  Multiplexer #(.select(3), .width(32), .enable("false")) multiplexer_6 (
    .in0(ByteSX), .in1(HalfSX), .in2(MemRead), .in4(ByteZX), .in5(HalfZX), .out(MemResult), .sel(funct3));  // open: in3, in6, in7
  mem DMEM (.ReadData(MemRead), .WriteData(MemWrite), .WriteAddr(ALUResult), .clk(CLOCK), .MemRW(MemRW));

  // Other names for the same wires on the sheet: clk = CLOCK; fetch_addr[31:0] = FETCH_ADDRESS; rd[4:0] = inst[11:7];
  //   inst[14:12] = funct3; rs1[4:0] = inst[19:15]; rs2[4:0] = inst[24:20]; ByteOffset[1:0] = ALUResult[1:0];
  //   MemAddr[31:0] = ALUResult; HalfOffset = ALUResult[1]; R2[31:0] = MemWrite

  // Notes on the sheet:
  //   Output
  //   Inputs/Outputs from run.circ. DO NOT MOVE THESE.
  //   Inputs
  //   Inputs/Outputs from run.circ. DO NOT MOVE THESE.
endmodule

module control (
  input  BrEq,
  input  BrLt,
  input  [31:0] inst,
  output [2:0] ImmSel,
  output BrUn,
  output ASel,
  output BSel,
  output [3:0] ALUSel,
  output MemRW,
  output RegWEn,
  output [1:0] WBSel,
  output PCSel
);

  wire auipc, beq, beq_t, bgeu, bgeu_t, blt, blt_t, bltu, bltu_t, bne, bne_t, btype, comparator_1_eq,
       comparator_11_eq, comparator_12_eq, comparator_13_eq, comparator_14_eq, comparator_15_eq, itype, jal,
       jalr, load, logical, lui, not_1_out, not_2_out, rtype, utype;
  wire [1:0] ALUOpSel;
  wire [3:0] iALUOp, rALUOp;
  wire [3:3] and_1_out;

  Comparator #(.width(3), .mode("unsigned")) comparator_1 (
    .a(inst[14:12]), .b(3'b101), .eq(comparator_1_eq));  // open: gt, lt
  and and_1 (and_1_out[3], inst[30], comparator_1_eq);
  Comparator #(.width(7)) comparator_2 (.a(inst[6:0]), .b(7'b0110011), .eq(rtype));  // open: gt, lt
  Comparator #(.width(7)) comparator_3 (.a(inst[6:0]), .b(7'b0000011), .eq(load));  // open: gt, lt
  Comparator #(.width(7)) comparator_4 (.a(inst[6:0]), .b(7'b0010011), .eq(logical));  // open: gt, lt
  Comparator #(.width(7)) comparator_5 (.a(inst[6:0]), .b(7'b1100111), .eq(jalr));  // open: gt, lt
  Comparator #(.width(7)) comparator_6 (.a(inst[6:0]), .b(7'b0100011), .eq(MemRW));  // open: gt, lt
  Comparator #(.width(7)) comparator_7 (.a(inst[6:0]), .b(7'b1100011), .eq(btype));  // open: gt, lt
  Comparator #(.width(7)) comparator_8 (.a(inst[6:0]), .b(7'b0010111), .eq(auipc));  // open: gt, lt
  Comparator #(.width(7)) comparator_9 (.a(inst[6:0]), .b(7'b0110111), .eq(lui));  // open: gt, lt
  Comparator #(.width(7)) comparator_10 (.a(inst[6:0]), .b(7'b1101111), .eq(jal));  // open: gt, lt
  ROM #(.addrWidth(5), .dataWidth(4)) rtypeALUSel (.addr({inst[30], inst[25], inst[14:12]}), .data(rALUOp));
  ROM #(.addrWidth(4), .dataWidth(4)) itypeALUSel (.addr({and_1_out[3], inst[14:12]}), .data(iALUOp));
  Comparator #(.width(3)) comparator_11 (.a(inst[14:12]), .b(3'b000), .eq(comparator_11_eq));  // open: gt, lt
  and and_2 (beq, comparator_11_eq, btype);
  Comparator #(.width(3)) comparator_12 (.a(inst[14:12]), .b(3'b100), .eq(comparator_12_eq));  // open: gt, lt
  and and_3 (blt, comparator_12_eq, btype);
  Comparator #(.width(3)) comparator_13 (.a(inst[14:12]), .b(3'b110), .eq(comparator_13_eq));  // open: gt, lt
  and and_4 (bltu, comparator_13_eq, btype);
  Comparator #(.width(3)) comparator_14 (.a(inst[14:12]), .b(3'b001), .eq(comparator_14_eq));  // open: gt, lt
  and and_5 (bne, comparator_14_eq, btype);
  Comparator #(.width(3)) comparator_15 (.a(inst[14:12]), .b(3'b111), .eq(comparator_15_eq));  // open: gt, lt
  and and_6 (bgeu, comparator_15_eq, btype);
  // Probe on ALUOpSel
  Priority_Encoder #(.select(2)) priority_encoder_1 (
    .in0(1'b1), .in1(logical), .in2(rtype), .out(ALUOpSel), .en_in(1'b1));  // open: in3, gs, en_out
  or or_1 (itype, load, logical, jalr);
  or or_2 (utype, auipc, lui);
  and and_7 (beq_t, beq, BrEq);
  and and_8 (blt_t, blt, BrLt);
  and and_9 (bltu_t, bltu, BrLt);
  and and_10 (bne_t, bne, not_1_out);
  not not_1 (not_1_out, BrEq);
  and and_11 (bgeu_t, bgeu, not_2_out);
  not not_2 (not_2_out, BrLt);
  Priority_Encoder priority_encoder_2 (
    .in0(itype), .in1(MemRW), .in2(btype), .in3(utype), .in4(jal), .out(ImmSel), .en_in(1'b1));  // open: in5, in6, in7, gs, en_out
  and and_12 (BrUn, inst[13], btype);
  or or_3 (ASel, btype, auipc, jal);
  not not_3 (BSel, rtype);
  Multiplexer #(.select(2), .width(4), .enable("false")) multiplexer_1 (
    .in0(4'b0011), .in1(iALUOp), .in2(rALUOp), .out(ALUSel), .sel(ALUOpSel));  // open: in3
  or or_4 (RegWEn, rtype, itype, utype, jal);
  or or_5 (WBSel[0], rtype, logical, utype);
  or or_6 (WBSel[1], jalr, jal);
  or or_7 (PCSel, beq_t, blt_t, bltu_t, bne_t, bgeu_t, jalr, jal);

  // Other names for the same wires on the sheet: funct7[6:0] = inst[31:25]; funct3[2:0] = inst[14:12];
  //   opcode[6:0] = inst[6:0]; stype = MemRW

  // Notes on the sheet:
  //   contents of rtypeALUSel (hex, n*v repeats v):
  //   3 c d 0 2 a 1 0 5 7 0 6 0 8 0 9 4
  //   contents of itypeALUSel (hex, n*v repeats v):
  //   3 c d 0 2 a 1 6*0 b
endmodule

module immgen (
  input  [31:0] inst,
  input  [2:0] ImmSel,
  output [31:0] imm
);

  wire [31:0] B, I, J, S;

  Multiplexer #(.select(3), .width(32), .enable("false")) multiplexer_1 (
    .in0(I), .in1(S), .in2(B), .in3({inst[31:12], {12{1'b0}}}), .in4(J), .out(imm), .sel(ImmSel));  // open: in5, in6, in7
  assign I = {{20{inst[31]}}, inst[31:20]};  // Bit_Extender bit_extender_1
  assign S = {{20{inst[31]}}, {inst[31:25], inst[11:7]}};  // Bit_Extender bit_extender_2
  assign B = {{19{inst[31]}}, {inst[31], inst[7], inst[30:25], inst[11:8], 1'b0}};  // Bit_Extender bit_extender_3
  assign J = {{11{inst[31]}}, {inst[31], inst[19:12], inst[20], inst[30:21], 1'b0}};  // Bit_Extender bit_extender_4
  // Probe on I
  // Probe on S
  // Probe on B
  // Probe on {inst[31:12], {12{1'b0}}}
  // Probe on J

  // Other names for the same wires on the sheet: imm11_7[4:0] = inst[11:7]; imm11_8[3:0] = inst[11:8]; imm7 = inst[7];
  //   imm30_21[9:0] = inst[30:21]; imm31_12[19:0] = inst[31:12]; imm31_20[11:0] = inst[31:20]; U[31:12] = inst[31:12];
  //   imm30_25[5:0] = inst[30:25]; imm31_25[6:0] = inst[31:25]; imm20 = inst[20]; imm19_12[7:0] = inst[19:12];
  //   imm31 = inst[31]
endmodule

module brcomp (
  input  [31:0] A,
  input  [31:0] B,
  input  BrUn,
  output BrEQ,
  output BrLt
);

  wire BrLt_t, BrLtu;

  Comparator #(.width(32)) comparator_1 (.a(A), .b(B), .eq(BrEQ));  // open: gt, lt
  Comparator #(.width(32)) comparator_2 (.a(A), .b(B), .lt(BrLt_t));  // open: gt, eq
  Comparator #(.width(32), .mode("unsigned")) comparator_3 (.a(A), .b(B), .lt(BrLtu));  // open: gt, eq
  Multiplexer #(.enable("false")) multiplexer_1 (.in0(BrLt_t), .in1(BrLtu), .out(BrLt), .sel(BrUn));
endmodule
